// Digital circuit FA-CL.dig as structural Verilog
module FA_CL (
  input  A,
  input  B,
  input  C,
  output Prop,
  output Gen,
  output Sum
);

  wire and_2_out, and_3_out, and_4_out, and_5_out, not_1_out, not_2_out, not_3_out;

  not not_1 (not_1_out, A);
  not not_2 (not_2_out, B);
  not not_3 (not_3_out, C);
  or or_1 (Prop, A, B);
  and and_1 (Gen, A, B);
  and and_2 (and_2_out, not_1_out, not_2_out, C);
  and and_3 (and_3_out, not_1_out, B, not_3_out);
  and and_4 (and_4_out, A, not_2_out, not_3_out);
  and and_5 (and_5_out, A, B, C);
  or or_2 (Sum, and_2_out, and_3_out, and_4_out, and_5_out);
endmodule
