// Digital circuit Q1_230313.dig as structural Verilog
module Q1_230313 (
  input  A0,
  input  A1,
  input  A2,
  input  A3,
  input  B0,
  input  B1,
  input  B2,
  input  B3,
  input  Sub
);

  wire fasub_4bit_1_s0, fasub_4bit_1_s1, fasub_4bit_1_s2, fasub_4bit_1_s3, plus_minus_seven_1_a1,
       plus_minus_seven_1_a2, plus_minus_seven_1_b1, plus_minus_seven_1_b2, plus_minus_seven_1_c1,
       plus_minus_seven_1_c2, plus_minus_seven_1_d1, plus_minus_seven_1_d2, plus_minus_seven_1_e1,
       plus_minus_seven_1_e2, plus_minus_seven_1_f1, plus_minus_seven_1_f2, plus_minus_seven_1_g1,
       plus_minus_seven_1_g2;

  FASub_4bit fasub_4bit_1 (
    .A0(A0), .A1(A1), .A2(A2), .A3(A3), .B0(B0), .B1(B1), .B2(B2), .B3(B3), .Subtraction(Sub),
    .S0(fasub_4bit_1_s0), .S1(fasub_4bit_1_s1), .S2(fasub_4bit_1_s2), .S3(fasub_4bit_1_s3));  // open: Overflow
  plus_minus_seven plus_minus_seven_1 (
    .S0(fasub_4bit_1_s0), .S1(fasub_4bit_1_s1), .S2(fasub_4bit_1_s2), .S3(fasub_4bit_1_s3),
    .a1(plus_minus_seven_1_a1), .b1(plus_minus_seven_1_b1), .c1(plus_minus_seven_1_c1),
    .d1(plus_minus_seven_1_d1), .e1(plus_minus_seven_1_e1), .f1(plus_minus_seven_1_f1),
    .g1(plus_minus_seven_1_g1), .a2(plus_minus_seven_1_a2), .b2(plus_minus_seven_1_b2),
    .c2(plus_minus_seven_1_c2), .d2(plus_minus_seven_1_d2), .e2(plus_minus_seven_1_e2),
    .f2(plus_minus_seven_1_f2), .g2(plus_minus_seven_1_g2));
  Seven_Seg seven_seg_1 (
    .a(plus_minus_seven_1_a1), .b(plus_minus_seven_1_b1), .c(plus_minus_seven_1_c1),
    .d(plus_minus_seven_1_d1), .e(plus_minus_seven_1_e1), .f(plus_minus_seven_1_f1),
    .g(plus_minus_seven_1_g1), .dp(1'b0));
  Seven_Seg seven_seg_2 (
    .a(plus_minus_seven_1_a2), .b(plus_minus_seven_1_b2), .c(plus_minus_seven_1_c2),
    .d(plus_minus_seven_1_d2), .e(plus_minus_seven_1_e2), .f(plus_minus_seven_1_f2),
    .g(plus_minus_seven_1_g2), .dp(1'b0));
endmodule
