// Digital circuit hw_2_decoder_1-bit_comparator.dig as structural Verilog
module hw_2_decoder_1_bit_comparator (
  input  ci0,
  input  ci1,
  input  xi,
  input  yi,
  output c_i_plus_1_0,
  output c_i_plus_1_1
);

  wire decoder_1_out_1, decoder_1_out_2, decoder_1_out_4, decoder_1_out_5, decoder_1_out_6, decoder_1_out_7,
       decoder_1_out_8, decoder_1_out_9, decoder_1_out_10, decoder_1_out_11;

  Decoder #(.Selector_Bits(4)) decoder_1 (
    .sel({ci0, ci1, xi, yi}), .out_1(decoder_1_out_1), .out_2(decoder_1_out_2), .out_4(decoder_1_out_4),
    .out_5(decoder_1_out_5), .out_6(decoder_1_out_6), .out_7(decoder_1_out_7), .out_8(decoder_1_out_8),
    .out_9(decoder_1_out_9), .out_10(decoder_1_out_10), .out_11(decoder_1_out_11));  // open: out_0, out_3, out_12, out_13, out_14, out_15
  or or_1 (c_i_plus_1_0, decoder_1_out_11, decoder_1_out_10, decoder_1_out_8, decoder_1_out_6, decoder_1_out_2);
  or or_2 (c_i_plus_1_1, decoder_1_out_9, decoder_1_out_7, decoder_1_out_5, decoder_1_out_4, decoder_1_out_1);
endmodule
