// Digital circuit ABFlipFlop.dig as structural Verilog
module ABFlipFlop (
  input  A,
  input  B,
  input  CLK,
  output Q,
  output out_5
);

  wire and_1_out, and_2_out, not_1_out;

  not not_1 (not_1_out, B);
  and and_1 (and_1_out, out_5, A);
  and and_2 (and_2_out, not_1_out, Q);
  SRFlipFlop srflipflop_1 (.S(and_1_out), .CLK(CLK), .R(and_2_out), .Q(Q), .Q_2(out_5));

  // Notes on the sheet:
  //   JK Flip-Flop
endmodule
