// Digital circuit JKFlipFlop.dig as structural Verilog
module JKFlipFlop (
  input  J,
  input  K,
  input  CLK,
  output Q,
  output Q_2
);

  wire and_1_out, and_2_out, and_3_out, and_4_out, not_1_out, srlatch_1_p3, srlatch_1_p4;

  not not_1 (not_1_out, CLK);
  and and_1 (and_1_out, Q_2, J, not_1_out);
  and and_2 (and_2_out, not_1_out, K, Q);
  // SRLatch srlatch_1: pin names not known; wires that end beside it: and_1_out, and_2_out, srlatch_1_p3, srlatch_1_p4
  and and_3 (and_3_out, srlatch_1_p3, CLK);
  and and_4 (and_4_out, srlatch_1_p4, CLK);
  // SRLatch srlatch_2: pin names not known; wires that end beside it: and_3_out, and_4_out, Q, Q_2
endmodule
