// Digital circuit prac_jk_ab_ff.dig as structural Verilog
module prac_jk_ab_ff (
  input  A_J,
  input  B_K,
  input  CLK,
  output Qnext,
  output Q,
  output Qnext_2
);

  wire RN_out, SN_out;

  Button #(.activeLow("true")) SN (.out(SN_out));
  Button #(.activeLow("true")) RN (.out(RN_out));
  ABFF #(.applicationType("GHDL")) u_ABFF (.A(A_J), .B(B_K), .CLK(CLK), .Q_next(Qnext_2));
  JKFF #(.applicationType("GHDL")) u_JKFF (.SN(SN_out), .RN(RN_out), .J(A_J), .K(B_K), .CLK(CLK), .Q(Qnext), .QN(Q));
endmodule

/* Code of ABFF:
LIBRARY ieee;
USE ieee.std_logic_1164.all;
USE ieee.numeric_std.all;

entity ABFF is
    port(
        A, B, CLK: in std_logic;
        Q_next: out std_logic
    );
end ABFF;

architecture ABFF1 of ABFF is
    signal Qint: std_logic; -- internal value of Q
    signal input: std_logic_vector(0 to 1);

    begin
        input <= A & B;
        Q_next <= Qint;

        -- Q_next <= Qint; -- output Q and QN to port

        process(CLK) -- seems this is necessary for using "if-else"
        begin
            if CLK'event and CLK = '1' then -- rising edge of CLK
                -- Qint <= (A and not Qint) or (not B and Qint);
                Qint <=
                    '0' when input = "00" else
                    Qint when input = "01" else
                    not Qint when input = "10" else
                    '1' when input = "11";
            end if;
        end process;
end ABFF1;
*/

/* Code of JKFF:
LIBRARY ieee;
USE ieee.std_logic_1164.all;
USE ieee.numeric_std.all;

entity JKFF is
    port(
        SN, RN, J, K, CLK: in std_logic;
        Q, QN: out std_logic
    );
end JKFF;

architecture JKFF1 of JKFF is
    signal Qint: std_logic; -- internal value of Q

    begin
        Q <= Qint; -- output Q and QN to port
        QN <= not Qint;

        process(SN, RN, CLK) -- seems this is necessary for using "if-else"
        begin
            if RN = '0' then 
                Qint <= '0'; -- RN = '0' will clear the FF
            elsif SN = '0' then 
                Qint <= '1'; -- SN = '0' will set FF
            elsif CLK'event and CLK = '0' then -- falling edge of CLK
                Qint <= (J and not Qint) or (not K and Qint);
            end if;
        end process;
end JKFF1;
*/
