// Digital circuit BidirectionalShift.dig as structural Verilog
module BidirectionalShift (
  input  D0,
  input  D1,
  input  D2,
  input  D3,
  input  LSH,
  input  RSH,
  input  L,
  input  CLK,
  input  Si,
  output Q0,
  output Q1,
  output Q2,
  output Q3
);

  BidirectionalShift #(.applicationType("GHDL")) u_BidirectionalShift (
    .D({D3, D2, D1, D0}), .Si(Si), .LSh(LSH), .RSh(RSH), .L(L), .CLK(CLK), .Q({Q3, Q2, Q1, Q0}));
endmodule

/* Code of BidirectionalShift:
LIBRARY ieee;
USE ieee.std_logic_1164.all;
USE ieee.numeric_std.all;

entity BidirectionalShift is
    port(
        D: in std_logic_vector(3 downto 0);
        Si: in std_logic;
        LSh, RSh, L: in std_logic;
        CLK: in std_logic;
        Q: out std_logic_vector(3 downto 0)
    );
end BidirectionalShift;

architecture Behavior of BidirectionalShift is
    signal prev_Q: std_logic_vector(3 downto 0);
    signal state: std_logic_vector(1 downto 0);
    begin
        state <= LSh & RSh;
        Q <= prev_Q;
        
        process(CLK)
        begin
            if (CLK'event and CLK='1') then
                if state & L = "001" then 
                    prev_Q <= D; 
                end if;

                if state = "10" then 
                    prev_Q <= prev_Q sll 1;
                    prev_Q(0) <= Si;
                elsif state = "01" then 
                    prev_Q <= prev_Q srl 1;
                    prev_Q(3) <= Si;
                else
                    -- prev_Q <= prev_Q;
                end if;
            end if;
        end process;
    end Behavior;
*/
