// Digital circuit BidirectionalShiftLayout.dig as structural Verilog
module BidirectionalShiftLayout (
  input  RSh,
  input  L,
  input  CLK,
  input  SI,
  input  D3,
  input  D2,
  input  D0,
  input  D1,
  input  LSh,
  output Q0,
  output Q1,
  output Q2,
  output Q3
);

  wire multiplexer_1_out, multiplexer_2_out, multiplexer_3_out, multiplexer_4_out;

  Multiplexer #(.Selector_Bits(3)) multiplexer_1 (
    .sel({LSh, RSh, L}), .in_0(Q3), .in_1(D3), .in_2(SI), .in_3(SI), .in_4(Q2), .in_5(Q2), .in_6(Q3),
    .in_7(Q3), .out(multiplexer_1_out));
  D_FF d_ff_1 (.D(multiplexer_1_out), .C(CLK), .Q(Q3));  // open: nQ
  Multiplexer #(.Selector_Bits(3)) multiplexer_2 (
    .sel({LSh, RSh, L}), .in_0(Q2), .in_1(D2), .in_2(Q3), .in_3(Q3), .in_4(Q1), .in_5(Q1), .in_6(Q2),
    .in_7(Q2), .out(multiplexer_2_out));
  D_FF d_ff_2 (.D(multiplexer_2_out), .C(CLK), .Q(Q2));  // open: nQ
  Multiplexer #(.Selector_Bits(3)) multiplexer_3 (
    .sel({LSh, RSh, L}), .in_0(Q1), .in_1(D1), .in_2(Q2), .in_3(Q2), .in_4(Q0), .in_5(Q0), .in_6(Q1),
    .in_7(Q1), .out(multiplexer_3_out));
  D_FF d_ff_3 (.D(multiplexer_3_out), .C(CLK), .Q(Q1));  // open: nQ
  Multiplexer #(.Selector_Bits(3)) multiplexer_4 (
    .sel({LSh, RSh, L}), .in_0(Q0), .in_1(D0), .in_2(Q1), .in_3(Q1), .in_4(SI), .in_5(SI), .in_6(Q0),
    .in_7(Q0), .out(multiplexer_4_out));
  D_FF d_ff_4 (.D(multiplexer_4_out), .C(CLK), .Q(Q0));  // open: nQ
endmodule
