// Digital circuit Q2.dig as structural Verilog
module Q2 (
  input  Select_A_B,
  input  Enable,
  input  CLK,
  input  Cin,
  input  Mode,
  input  Enable_2,
  input  in_8,
  input  [3:0] Input,
  input  [1:0] Address,
  input  Chip,
  input  Write,
  input  Read,
  output Overflow_Warning
);

  wire [3:0] addersubber_1_p11, demultiplexer_1_out_0, demultiplexer_1_out_1, multiplexer_1_out,
       register_1_q, register_2_q, u_SRAM4bits_do;

  Demultiplexer #(.Bits(4)) demultiplexer_1 (
    .sel(Select_A_B), .in(u_SRAM4bits_do), .out_0(demultiplexer_1_out_0), .out_1(demultiplexer_1_out_1));
  Register #(.Bits(4)) register_1 (.D(demultiplexer_1_out_0), .C(CLK), .en(Enable), .Q(register_1_q));
  // AdderSubber addersubber_1: pin names not known; wires that end beside it: register_1_q[0], register_1_q[1], register_1_q[2], register_1_q[3], demultiplexer_1_out_1[0], demultiplexer_1_out_1[1], demultiplexer_1_out_1[2], demultiplexer_1_out_1[3], Cin, Mode, addersubber_1_p11[0], addersubber_1_p11[1], addersubber_1_p11[2], addersubber_1_p11[3], Overflow_Warning
  Register #(.Bits(4)) register_2 (.D(addersubber_1_p11), .C(CLK), .en(Enable_2), .Q(register_2_q));
  Multiplexer #(.Bits(4)) multiplexer_1 (.sel(in_8), .in_0(Input), .in_1(register_2_q), .out(multiplexer_1_out));
  SRAM4bits #(.applicationType("GHDL")) u_SRAM4bits (
    .D(multiplexer_1_out), .Address(Address), .ChipSelect(Chip), .WE(Write), .OE(Read), .DO(u_SRAM4bits_do));
endmodule

/* Code of SRAM4bits:
LIBRARY ieee;
USE ieee.std_logic_1164.all;
USE ieee.numeric_std.all;

entity SRAM4bits is
    port(
        D: in std_logic_vector(3 downto 0);
        Address: in std_logic_vector(1 downto 0);
        ChipSelect, WE, OE: in std_logic;
        DO: out std_logic_vector(3 downto 0)
    );
end SRAM4bits;

architecture Behavior of SRAM4bits is
    type memory is array(3 downto 0) of std_logic_vector(3 downto 0);
    signal SRAM_internal: memory := ("0000", "0000", "0000", "0000");
    signal Address_int: integer;
    signal Address_temp: std_logic_vector(3 downto 0);

    begin
        Address_temp <= "00" & Address;
        Address_int <= to_integer(unsigned(Address_temp));

        -- Read memory
        DO <= "ZZZZ" when ChipSelect = '0'
        else "ZZZZ" when OE = '0'
        else SRAM_internal(Address_int) when OE = '1';

        -- Write memory
        SRAM_internal(Address_int) <= D when WE = '1';

    end Behavior;
*/
