// Digital circuit SRAM4Bits.dig as structural Verilog
module SRAM4Bits (
  input  [1:0] in_1,
  input  in_2,
  input  [3:0] in_3,
  input  in_4,
  input  in_5,
  output [3:0] out_6
);

  SRAM4bits #(.applicationType("GHDL")) u_SRAM4bits (
    .D(in_3), .Address(in_1), .ChipSelect(in_2), .WE(in_4), .OE(in_5), .DO(out_6));
endmodule

/* Code of SRAM4bits:
LIBRARY ieee;
USE ieee.std_logic_1164.all;
USE ieee.numeric_std.all;

entity SRAM4bits is
    port(
        D: in std_logic_vector(3 downto 0);
        Address: in std_logic_vector(1 downto 0);
        ChipSelect, WE, OE: in std_logic;
        DO: out std_logic_vector(3 downto 0)
    );
end SRAM4bits;

architecture Behavior of SRAM4bits is
    type memory is array(3 downto 0) of std_logic_vector(3 downto 0);
    signal SRAM_internal: memory := ("0000", "0000", "0000", "0000");
    signal Address_int: integer;
    signal Address_temp: std_logic_vector(3 downto 0);

    begin
        Address_temp <= "00" & Address;
        Address_int <= to_integer(unsigned(Address_temp));

        -- Read memory
        DO <= "ZZZZ" when ChipSelect = '0'
        else "ZZZZ" when OE = '0'
        else SRAM_internal(Address_int) when OE = '1';

        -- Write memory
        SRAM_internal(Address_int) <= D when WE = '1';

    end Behavior;
*/
