// Digital circuit dig_my_state_machine.dig as structural Verilog
module dig_my_state_machine (
  input  X,
  input  clk,
  output B,
  output A,
  output Z
);

  wire and_1_out, and_2_out, and_3_out, and_4_out, not_1_out, not_2_out, not_3_out, not_4_out, or_1_out,
       or_2_out;

  not not_1 (not_1_out, X);
  not not_2 (not_2_out, A);
  not not_3 (not_3_out, B);
  and and_1 (and_1_out, A, X);
  and and_2 (and_2_out, X, B);
  and and_3 (and_3_out, not_2_out, not_3_out, X);
  or or_1 (or_1_out, and_1_out, and_2_out);
  or or_2 (or_2_out, and_1_out, and_3_out);
  T_FF T0 (.T(or_1_out), .C(clk), .Q(A));  // open: nQ
  T_FF T1 (.T(or_2_out), .C(clk), .Q(B));  // open: nQ
  not not_4 (not_4_out, A);
  and and_4 (and_4_out, not_1_out, not_4_out, B);
  or or_3 (Z, and_1_out, and_4_out, and_3_out);
endmodule
