// Digital circuit dig_q1_my_counter_circuit.dig as structural Verilog
module dig_q1_my_counter_circuit (
  input  CLK,
  output C,
  output B,
  output A
);

  wire and_1_out, and_2_out, and_3_out, and_4_out, not_1_out, not_2_out, not_3_out, or_1_out, or_2_out,
       or_3_out;

  not not_1 (not_1_out, C);
  not not_2 (not_2_out, B);
  not not_3 (not_3_out, A);
  and and_1 (and_1_out, not_2_out, not_3_out);
  and and_2 (and_2_out, A, B);
  or or_1 (or_1_out, not_3_out, not_1_out);
  and and_3 (and_3_out, not_1_out, not_2_out);
  and and_4 (and_4_out, B, C);
  or or_2 (or_2_out, and_1_out, and_2_out);
  or or_3 (or_3_out, and_3_out, and_4_out);
  JK_FF u_C (.J(not_2_out), .C(CLK), .K(or_2_out), .Q(C));  // open: nQ
  JK_FF u_B (.J(or_1_out), .C(CLK), .K(1'b1), .Q(B));  // open: nQ
  JK_FF u_A (.J(or_3_out), .C(CLK), .K(not_2_out), .Q(A));  // open: nQ
endmodule
