// Digital circuit dig_q2_fsm_circuit.dig as structural Verilog
module dig_q2_fsm_circuit (
  input  X,
  input  CLK,
  output C,
  output B,
  output A
);

  wire and_1_out, and_2_out, and_3_out, and_4_out, and_5_out, not_1_out, not_2_out, not_3_out, not_4_out,
       or_1_out, or_2_out, or_3_out;

  not not_1 (not_1_out, X);
  not not_2 (not_2_out, C);
  not not_3 (not_3_out, B);
  not not_4 (not_4_out, A);
  and and_1 (and_1_out, A, B, not_1_out);
  and and_2 (and_2_out, B, not_1_out);
  and and_3 (and_3_out, C, not_1_out);
  and and_4 (and_4_out, X, not_2_out, not_3_out);
  and and_5 (and_5_out, not_4_out, not_2_out, X);
  or or_1 (or_1_out, and_1_out, C);
  or or_2 (or_2_out, and_2_out, and_3_out, and_4_out, A);
  or or_3 (or_3_out, and_5_out, B, not_1_out);
  T_FF u_C (.T(or_1_out), .C(CLK), .Q(C));  // open: nQ
  T_FF u_B (.T(or_2_out), .C(CLK), .Q(B));  // open: nQ
  T_FF u_A (.T(or_3_out), .C(CLK), .Q(A));  // open: nQ
endmodule
