// Digital circuit AdderSubber.dig as structural Verilog
module AdderSubber (
  input  A0,
  input  A1,
  input  A2,
  input  A3,
  input  B0,
  input  B1,
  input  B2,
  input  B3,
  input  Carry_in,
  input  Mode,
  output X0,
  output X1,
  output X2,
  output X3,
  output Overflow
);

  wire u_AdderSubber_2_cout, u_AdderSubber_3_cout, u_AdderSubber_4_cout;

  AdderSubber #(.applicationType("GHDL")) u_AdderSubber (
    .A(A3), .B(B3), .Cin(u_AdderSubber_2_cout), .Sub(Mode), .Cout(Overflow), .Sum(X3));
  AdderSubber #(.applicationType("GHDL")) u_AdderSubber_2 (
    .A(A2), .B(B2), .Cin(u_AdderSubber_3_cout), .Sub(Mode), .Cout(u_AdderSubber_2_cout), .Sum(X2));
  AdderSubber #(.applicationType("GHDL")) u_AdderSubber_3 (
    .A(A1), .B(B1), .Cin(u_AdderSubber_4_cout), .Sub(Mode), .Cout(u_AdderSubber_3_cout), .Sum(X1));
  AdderSubber #(.applicationType("GHDL")) u_AdderSubber_4 (
    .A(A0), .B(B0), .Cin(Carry_in), .Sub(Mode), .Cout(u_AdderSubber_4_cout), .Sum(X0));
endmodule

/* Code of AdderSubber:
LIBRARY ieee;
USE ieee.std_logic_1164.all;
USE ieee.numeric_std.all;

entity AdderSubber is
    port  (
        A, B, Cin, Sub: in std_logic;
        Cout, Sum: out std_logic
    );
end AdderSubber;

architecture Equations of AdderSubber is
    begin   
        -- concurrent assignment statements
        Cout <= (A and B and not Sub) or (A and Cin and not Sub) or (not A and B and Sub) or (not A and Cin and Sub) or (B and Cin);
        Sum <= (not A and B and not Cin) or (A and not B and not Cin) or (not A and not B and Cin) or (A and B and Cin);
    end Equations;
*/
