// Digital circuit sequential_detector_circuit.dig as structural Verilog
module sequential_detector_circuit (
  input  CLK,
  input  X,
  output B,
  output C,
  output A,
  output Z
);

  wire and_2_out, and_3_out, and_4_out, and_5_out, and_6_out, not_1_out, not_2_out, not_3_out, not_4_out,
       or_1_out, or_2_out;

  not not_1 (not_1_out, A);
  not not_2 (not_2_out, X);
  not not_3 (not_3_out, B);
  not not_4 (not_4_out, C);
  and and_1 (Z, X, B, C);
  and and_2 (and_2_out, not_2_out, A);
  and and_3 (and_3_out, not_2_out, not_3_out, C);
  and and_4 (and_4_out, not_2_out, B, not_4_out);
  and and_5 (and_5_out, X, not_1_out, not_3_out);
  and and_6 (and_6_out, B, not_4_out);
  or or_1 (or_1_out, and_2_out, and_3_out, and_4_out);
  or or_2 (or_2_out, and_5_out, and_6_out);
  D_FF u_A (.D(Z), .C(CLK), .Q(A));  // open: nQ
  D_FF u_B (.D(or_1_out), .C(CLK), .Q(B));  // open: nQ
  D_FF u_C (.D(or_2_out), .C(CLK), .Q(C));  // open: nQ
endmodule
