// Digital circuit dig_q1_my_counter_circuit.dig as structural Verilog
module dig_q1_my_counter_circuit (
  input  clk,
  output Q0,
  output Q1,
  output Q2
);

  wire and_1_out, and_2_out, and_3_out, and_4_out, and_5_out, and_6_out, not_1_out, not_2_out, not_3_out,
       or_1_out, or_2_out, or_3_out;

  not not_1 (not_1_out, Q0);
  not not_2 (not_2_out, Q1);
  not not_3 (not_3_out, Q2);
  and and_1 (and_1_out, not_1_out, not_2_out);
  and and_2 (and_2_out, not_2_out, not_3_out);
  and and_3 (and_3_out, Q1, Q2);
  and and_4 (and_4_out, not_1_out, not_2_out);
  and and_5 (and_5_out, Q0, Q1, not_3_out);
  and and_6 (and_6_out, not_2_out, Q2);
  or or_1 (or_1_out, and_1_out, and_2_out, and_3_out);
  or or_2 (or_2_out, not_1_out, Q1, not_3_out);
  or or_3 (or_3_out, and_4_out, and_5_out, and_6_out);
  JK_FF JK0 (.J(or_1_out), .C(clk), .K(or_1_out), .Q(Q0));  // open: nQ
  JK_FF JK1 (.J(or_2_out), .C(clk), .K(or_2_out), .Q(Q1));  // open: nQ
  JK_FF JK2 (.J(or_3_out), .C(clk), .K(or_3_out), .Q(Q2));  // open: nQ
endmodule
