// Digital circuit serial_adder_vhdl.dig as structural Verilog
module serial_adder_vhdl (
  input  [3:0] X,
  input  Si,
  input  Sh,
  input  Ld,
  input  CLK,
  output out_6
);

  LeftShifter #(.applicationType("GHDL")) u_LeftShifter (
    .D_X(X), .Si(Si), .Sh(Sh), .Load(Ld), .CLK(CLK), .x_out(out_6));
endmodule

/* Code of LeftShifter:
LIBRARY ieee;
USE ieee.std_logic_1164.all;
USE ieee.numeric_std.all;

entity LeftShifter is
    port(
        D_X: in std_logic_vector(3 downto 0);
        Si, Sh, Load: in std_logic;
        CLK: in std_logic;
        x_out: out std_logic
    );
end LeftShifter;

architecture Behavior of LeftShifter is
    signal prev_X: std_logic_vector(3 downto 0);
    signal state: std_logic_vector(1 downto 0);
    
    begin
        x_out <= prev_X(0);
        state <= Sh & Load;
        
        process(CLK)
        begin
            if (CLK'event and CLK='1') then
                -- Load input data
                if state = "01" then 
                    prev_X <= D_X; 
                end if;

                if Sh = '1' then 
                    prev_X <= prev_X sll 1;
                    prev_X(3) <= Si;
                end if;
            end if;
        end process;
    end Behavior;
*/
