// Digital circuit serial_adder_control.dig as structural Verilog
module serial_adder_control (
  input  St,
  input  CLK,
  output Sh
);

  wire and_1_out, and_2_out, D_A_q, D_B_q, not_1_out, not_2_out, not_3_out, or_1_out, or_2_out;

  not not_1 (not_1_out, St);
  not not_2 (not_2_out, D_A_q);
  not not_3 (not_3_out, D_B_q);
  or or_1 (or_1_out, D_A_q, D_B_q);
  and and_1 (and_1_out, D_A_q, not_3_out);
  and and_2 (and_2_out, St, not_3_out);
  or or_2 (or_2_out, and_1_out, and_2_out);
  D_FF D_A (.D(or_1_out), .C(CLK), .Q(D_A_q));  // open: nQ
  D_FF D_B (.D(or_2_out), .C(CLK), .Q(D_B_q));  // open: nQ
  or or_3 (Sh, D_A_q, D_B_q);
endmodule
