// Digital circuit RAMRegister9Bit_VHDL.dig as structural Verilog
module RAMRegister9Bit_VHDL (
  input  [3:0] Multiplier,
  input  [3:0] Multiplicand,
  input  Load,
  input  C4,
  input  CLK,
  input  Ad,
  input  Sh,
  output D0,
  output D1,
  output D2,
  output D3,
  output D4,
  output D5,
  output D6,
  output D7,
  output D8,
  output M
);

  RAMRegister9Bit #(.applicationType("GHDL")) u_RAMRegister9Bit (
    .D({C4, Multiplicand, Multiplier}), .Load(Load), .Sh(Sh), .Ad(Ad), .CLK(CLK),
    .DO({D8, D7, D6, D5, D4, D3, D2, D1, D0}), .M(M));
endmodule

/* Code of RAMRegister9Bit:
LIBRARY ieee;
USE ieee.std_logic_1164.all;
USE ieee.numeric_std.all;

entity RAMRegister9Bit is
    port(
        D: in std_logic_vector(8 downto 0);
        Load, Sh, Ad: in std_logic;
        CLK: in std_logic;
        DO: out std_logic_vector(8 downto 0);
        M: out std_logic
    );
end RAMRegister9Bit;

architecture Behavior of RAMRegister9Bit is
    signal SRAM_internal: std_logic_vector(8 downto 0) := ("000000000");

    begin
        process (CLK)
        begin
            DO <= SRAM_internal;
            M <= DO(0);
            if rising_edge(CLK) then
                -- Write memory
                SRAM_internal <= D when Load = '1';

                if Sh then
                    SRAM_internal <= SRAM_internal srl 1;
                end if;
            end if;
        end process;

    end Behavior;
*/
