// Digital circuit serial_adder_vhdl.dig as structural Verilog
module serial_adder_vhdl (
  input  [3:0] X,
  input  Ld,
  input  CLK,
  input  [3:0] y,
  input  St,
  output x_0,
  output x_1,
  output x_2,
  output x_3,
  output y_0,
  output y_1,
  output y_2,
  output y_3
);

  wire d_ff_1_q, serial_adder_control_1_sh, u_FullAdder_cout, u_FullAdder_sum, u_RightShifter_2_x_out,
       u_RightShifter_x_out;

  serial_adder_control serial_adder_control_1 (.St(St), .CLK(CLK), .Sh(serial_adder_control_1_sh));
  RightShifter #(.applicationType("GHDL")) u_RightShifter (
    .D_X(X), .Si(u_FullAdder_sum), .Sh(serial_adder_control_1_sh), .Load(Ld), .CLK(CLK),
    .x_out(u_RightShifter_x_out), .x_viz({x_3, x_2, x_1, x_0}));
  RightShifter #(.applicationType("GHDL")) u_RightShifter_2 (
    .D_X(y), .Si(u_RightShifter_2_x_out), .Sh(serial_adder_control_1_sh), .Load(Ld), .CLK(CLK),
    .x_out(u_RightShifter_2_x_out), .x_viz({y_3, y_2, y_1, y_0}));
  FullAdder #(.applicationType("GHDL")) u_FullAdder (
    .x(u_RightShifter_x_out), .y(u_RightShifter_2_x_out), .cin(d_ff_1_q), .clk(CLK), .sum(u_FullAdder_sum),
    .cout(u_FullAdder_cout));
  D_FF d_ff_1 (.D(u_FullAdder_cout), .C(CLK), .Q(d_ff_1_q));  // open: nQ
endmodule

/* Code of RightShifter:
LIBRARY ieee;
USE ieee.std_logic_1164.all;
USE ieee.numeric_std.all;

entity RightShifter is
    port(
        D_X: in std_logic_vector(3 downto 0);
        Si, Sh, Load: in std_logic;
        CLK: in std_logic;
        x_out: out std_logic;
        x_viz: out std_logic_vector(3 downto 0)
    );
end RightShifter;

architecture Behavior of RightShifter is
    signal prev_X: std_logic_vector(3 downto 0);
    signal state: std_logic_vector(1 downto 0);
    
    begin
        x_out <= prev_X(0);
        x_viz <= prev_X;
        state <= Sh & Load;
        
        process(CLK)
        begin
            if (CLK'event and CLK='1') then
                -- Load input data
                if state = "01" then 
                    prev_X <= D_X; 
                end if;

                if Sh = '1' then 
                    prev_X <= prev_X srl 1;
                    prev_X(3) <= Si;
                end if;
            end if;
        end process;
    end Behavior;
*/

/* Code of FullAdder:
library ieee;
use ieee.std_logic_1164.all;

entity FullAdder is
    port(
        x, y, cin, clk: in std_logic;
        sum, cout: out std_logic
    );
end entity;

architecture Behavioral of FullAdder is
    signal sum_temp, cout_temp: std_logic;
begin
    process(clk)
    begin
        if rising_edge(clk) then
            sum_temp <= x xor y xor cin;
            cout_temp <= (x and y) or (cin and (x xor y));
        end if;
    end process;

    sum <= sum_temp;
    cout <= cout_temp;
end architecture;
*/
