// Digital circuit FASub-4bit.dig as structural Verilog
module FASub_4bit (
  input  A0,
  input  A1,
  input  A2,
  input  A3,
  input  B0,
  input  B1,
  input  B2,
  input  B3,
  input  Subtraction,
  output S0,
  output S1,
  output S2,
  output S3,
  output Overflow
);

  wire fa_nocl_1_cout, fa_nocl_2_cout, fa_nocl_3_cout, xor_1_out, xor_2_out, xor_3_out, xor_4_out;

  xor xor_1 (xor_1_out, Subtraction, B0);
  FA_NOCL fa_nocl_1 (.A(A0), .B(xor_1_out), .Cin(Subtraction), .Cout(fa_nocl_1_cout), .Sum(S0));
  xor xor_2 (xor_2_out, Subtraction, B1);
  FA_NOCL fa_nocl_2 (.A(A1), .B(xor_2_out), .Cin(fa_nocl_1_cout), .Cout(fa_nocl_2_cout), .Sum(S1));
  xor xor_3 (xor_3_out, Subtraction, B2);
  FA_NOCL fa_nocl_3 (.A(A2), .B(xor_3_out), .Cin(fa_nocl_2_cout), .Cout(fa_nocl_3_cout), .Sum(S2));
  xor xor_4 (xor_4_out, Subtraction, B3);
  FA_NOCL fa_nocl_4 (.A(A3), .B(xor_4_out), .Cin(fa_nocl_3_cout), .Cout(Overflow), .Sum(S3));
endmodule
