// Digital circuit plus_minus_seven.dig as structural Verilog
module plus_minus_seven (
  input  S0,
  input  S1,
  input  S2,
  input  S3,
  output a1,
  output b1,
  output c1,
  output d1,
  output e1,
  output f1,
  output g1,
  output a2,
  output b2,
  output c2,
  output d2,
  output e2,
  output f2,
  output g2
);

  wire and_1_out, and_2_out, and_3_out, and_4_out, and_5_out, and_6_out, and_7_out, and_8_out, and_9_out,
       and_10_out, and_11_out, and_12_out, and_13_out, and_14_out, and_15_out, and_16_out, and_17_out,
       and_18_out, and_19_out, and_20_out, and_21_out, and_22_out, and_23_out, and_24_out, and_25_out,
       and_26_out, and_27_out, and_28_out, and_29_out, not_1_out, not_2_out, not_3_out, not_4_out;

  not not_1 (not_1_out, S3);
  not not_2 (not_2_out, S2);
  not not_3 (not_3_out, S1);
  not not_4 (not_4_out, S0);
  and and_1 (and_1_out, S0, S3);
  and and_2 (and_2_out, S1, S3);
  and and_3 (and_3_out, S2, S3);
  and and_4 (and_4_out, not_4_out, not_2_out);
  and and_5 (and_5_out, S0, S2);
  and and_6 (and_6_out, S0, S3);
  and and_7 (and_7_out, S1, not_1_out);
  and and_8 (and_8_out, not_4_out, not_3_out);
  and and_9 (and_9_out, S0, S1, S2);
  and and_10 (and_10_out, not_3_out, not_2_out);
  and and_11 (and_11_out, not_2_out, not_1_out);
  and and_12 (and_12_out, S2, S3);
  or or_1 (c2, S0, not_3_out, S2, S3);
  and and_13 (and_13_out, not_4_out, not_2_out);
  and and_14 (and_14_out, S0, not_3_out, S2);
  and and_15 (and_15_out, not_4_out, S1, not_1_out);
  and and_16 (and_16_out, S0, S1, S3);
  and and_17 (and_17_out, S1, not_2_out);
  and and_18 (and_18_out, not_4_out, not_2_out);
  and and_19 (and_19_out, not_4_out, S1, not_1_out);
  and and_20 (and_20_out, S0, S1, S2, S3);
  and and_21 (and_21_out, not_4_out, not_3_out);
  and and_22 (and_22_out, not_4_out, S2, not_1_out);
  and and_23 (and_23_out, S0, S1, S3);
  and and_24 (and_24_out, not_4_out, not_2_out, S3);
  and and_25 (and_25_out, not_3_out, S2, not_1_out);
  and and_26 (and_26_out, not_4_out, S1, not_1_out);
  and and_27 (and_27_out, not_4_out, not_3_out, S3);
  and and_28 (and_28_out, S1, not_2_out);
  and and_29 (and_29_out, not_3_out, S2);
  or or_2 (g1, and_1_out, and_2_out, and_3_out);
  or or_3 (e2, and_18_out, and_19_out, and_20_out);
  or or_4 (a2, and_4_out, and_5_out, and_6_out, and_7_out);
  or or_5 (b2, and_8_out, and_9_out, and_10_out, and_11_out, and_12_out);
  or or_6 (d2, and_13_out, and_14_out, and_15_out, and_16_out, and_17_out);
  or or_7 (f2, and_21_out, and_22_out, and_23_out, and_24_out, and_25_out);
  or or_8 (g2, and_26_out, and_27_out, and_28_out, and_29_out);

  assign a1 = 1'b0;
  assign b1 = 1'b0;
  assign c1 = 1'b0;
  assign d1 = 1'b0;
  assign e1 = 1'b0;
  assign f1 = 1'b0;
endmodule
