// Digital circuit hw_1_rom.dig as structural Verilog
module hw_1_rom (
  input  [3:0] A,
  input  sel,
  output [3:0] out
);

  ROM #(.AddrBits(4), .Bits(4)) ROM (.A(A), .sel(sel), .D(out));

  // Notes on the sheet:
  //   contents of ROM (hex, n*v repeats v):
  //   0,1,3,4,5,7,8,9,b,c
endmodule
