// Digital circuit SRFF.dig as structural Verilog
module SRFF (
  input  S,
  input  R,
  input  CLK,
  output Q,
  output Q_2
);

  wire and_1_out, and_2_out, and_3_out, and_4_out, not_1_out, sr_1_q, sr_1_q_2;

  not not_1 (not_1_out, CLK);
  and and_1 (and_1_out, S, not_1_out);
  and and_2 (and_2_out, not_1_out, R);
  SR sr_1 (.S(and_1_out), .R(and_2_out), .Q(sr_1_q), .Q_2(sr_1_q_2));
  and and_3 (and_3_out, sr_1_q, CLK);
  and and_4 (and_4_out, sr_1_q_2, CLK);
  SR sr_2 (.S(and_3_out), .R(and_4_out), .Q(Q), .Q_2(Q_2));
endmodule
