// Digital circuit dig_q2_fsm_circuit.dig as structural Verilog
module dig_q2_fsm_circuit (
  input  X,
  input  clk,
  output Q0,
  output Q1,
  output Q2
);

  wire and_1_out, and_2_out, and_3_out, and_4_out, and_5_out, not_1_out, not_2_out, not_3_out, not_4_out,
       not_5_out, or_1_out, or_2_out, or_3_out, or_4_out, or_5_out;

  not not_1 (not_1_out, X);
  not not_2 (not_2_out, Q0);
  not not_3 (not_3_out, Q1);
  not not_4 (not_4_out, Q0);
  not not_5 (not_5_out, Q2);
  and and_1 (and_1_out, not_1_out, Q1, Q2);
  and and_2 (and_2_out, Q0, not_1_out);
  and and_3 (and_3_out, not_2_out, not_3_out, X);
  and and_4 (and_4_out, Q1, not_1_out);
  and and_5 (and_5_out, not_4_out, not_5_out);
  or or_1 (or_1_out, Q0, and_1_out);
  or or_2 (or_2_out, and_2_out, and_3_out);
  or or_3 (or_3_out, and_4_out, Q2);
  T_FF T0 (.T(or_1_out), .C(clk), .Q(Q0));  // open: nQ
  or or_4 (or_4_out, or_2_out, or_3_out);
  or or_5 (or_5_out, and_5_out, Q1, not_1_out);
  T_FF T1 (.T(or_4_out), .C(clk), .Q(Q1));  // open: nQ
  T_FF T2 (.T(or_5_out), .C(clk), .Q(Q2));  // open: nQ
endmodule
