// Digital circuit Carry_Lookahead_wiki.dig as structural Verilog
module Carry_Lookahead_wiki (
  input  A0,
  input  A1,
  input  A2,
  input  A3,
  input  B0,
  input  B1,
  input  B2,
  input  B3,
  input  C0,
  output S0,
  output S1,
  output S2,
  output S3,
  output C4
);

  wire c1_2_c1, c1_3_c1, c1_4_c1, fa_cl_1_gen, fa_cl_1_prop, fa_cl_2_gen, fa_cl_2_prop, fa_cl_3_gen,
       fa_cl_3_prop, fa_cl_4_gen, fa_cl_4_prop;

  FA_CL fa_cl_1 (.A(A3), .B(B3), .C(c1_2_c1), .Prop(fa_cl_1_prop), .Gen(fa_cl_1_gen), .Sum(S3));
  c1 c1_1 (.P0(fa_cl_1_prop), .G0(fa_cl_1_gen), .C0(c1_2_c1), .C1(C4));
  FA_CL fa_cl_2 (.A(A2), .B(B2), .C(c1_3_c1), .Prop(fa_cl_2_prop), .Gen(fa_cl_2_gen), .Sum(S2));
  c1 c1_2 (.P0(fa_cl_2_prop), .G0(fa_cl_2_gen), .C0(c1_3_c1), .C1(c1_2_c1));
  FA_CL fa_cl_3 (.A(A1), .B(B1), .C(c1_4_c1), .Prop(fa_cl_3_prop), .Gen(fa_cl_3_gen), .Sum(S1));
  c1 c1_3 (.P0(fa_cl_3_prop), .G0(fa_cl_3_gen), .C0(c1_4_c1), .C1(c1_3_c1));
  FA_CL fa_cl_4 (.A(A0), .B(B0), .C(C0), .Prop(fa_cl_4_prop), .Gen(fa_cl_4_gen), .Sum(S0));
  c1 c1_4 (.P0(fa_cl_4_prop), .G0(fa_cl_4_gen), .C0(C0), .C1(c1_4_c1));
endmodule
