// Digital circuit FA-4bit.dig as structural Verilog
module FA_4bit (
  input  A0,
  input  A1,
  input  A2,
  input  A3,
  input  B0,
  input  B1,
  input  B2,
  input  B3,
  input  C0,
  output S3,
  output S2,
  output S1,
  output S0,
  output C4
);

  wire fa_nocl_2_cout, fa_nocl_3_cout, fa_nocl_4_cout;

  FA_NOCL fa_nocl_1 (.A(A3), .B(B3), .Cin(fa_nocl_2_cout), .Cout(C4), .Sum(S3));
  FA_NOCL fa_nocl_2 (.A(A2), .B(B2), .Cin(fa_nocl_3_cout), .Cout(fa_nocl_2_cout), .Sum(S2));
  FA_NOCL fa_nocl_3 (.A(A1), .B(B1), .Cin(fa_nocl_4_cout), .Cout(fa_nocl_3_cout), .Sum(S1));
  FA_NOCL fa_nocl_4 (.A(A0), .B(B0), .Cin(C0), .Cout(fa_nocl_4_cout), .Sum(S0));
endmodule
