// Digital circuit c1.dig as structural Verilog
module c1 (
  input  P0,
  input  G0,
  input  C0,
  output C1
);

  wire and_1_out;

  and and_1 (and_1_out, C0, P0);
  or or_1 (C1, and_1_out, G0);
endmodule
