// Digital circuit hw_1_nand.dig as structural Verilog
module hw_1_nand (
  input  A,
  input  B,
  input  C,
  input  D,
  output W,
  output X,
  output Y,
  output Z
);

  wire nand_1_out, nand_2_out, nand_3_out, nand_4_out, nand_5_out, nand_6_out, nand_7_out, nand_8_out,
       nand_9_out, nand_10_out, nand_11_out, nand_12_out, not_1_out, not_2_out, not_3_out, not_4_out;

  not not_1 (not_1_out, A);
  not not_2 (not_2_out, B);
  not not_3 (not_3_out, C);
  not not_4 (not_4_out, D);
  nand nand_1 (nand_1_out, B, C);
  nand nand_2 (nand_2_out, A, D);
  nand nand_3 (nand_3_out, not_2_out, C, D);
  nand nand_4 (nand_4_out, B, not_3_out);
  nand nand_5 (nand_5_out, A, not_4_out);
  nand nand_6 (nand_6_out, not_2_out, C, not_4_out);
  nand nand_7 (nand_7_out, B, not_3_out, D);
  nand nand_8 (nand_8_out, not_1_out, not_3_out, D);
  nand nand_9 (nand_9_out, A, not_4_out);
  nand nand_10 (nand_10_out, not_2_out, C, not_4_out);
  nand nand_11 (nand_11_out, B, not_3_out);
  nand nand_12 (nand_12_out, B, D);
  nand nand_13 (W, not_1_out, nand_1_out);
  nand nand_14 (X, nand_2_out, nand_3_out, nand_4_out);
  nand nand_15 (Y, nand_5_out, nand_6_out, nand_7_out);
  nand nand_16 (Z, nand_8_out, nand_9_out, nand_10_out, nand_11_out, nand_12_out);
endmodule
