// Digital circuit hw_2_decoder.dig as structural Verilog
module hw_2_decoder (
  input  x3,
  input  x2,
  input  x1,
  input  x0,
  input  y3,
  input  y2,
  input  y1,
  input  y0,
  input  c01,
  input  c00,
  output c41,
  output c40
);

  wire hw_2_decoder_1_bit_comparator_2_c_i_plus_1_0, hw_2_decoder_1_bit_comparator_2_c_i_plus_1_1,
       hw_2_decoder_1_bit_comparator_3_c_i_plus_1_0, hw_2_decoder_1_bit_comparator_3_c_i_plus_1_1,
       hw_2_decoder_1_bit_comparator_4_c_i_plus_1_0, hw_2_decoder_1_bit_comparator_4_c_i_plus_1_1;

  hw_2_decoder_1_bit_comparator hw_2_decoder_1_bit_comparator_1 (
    .ci0(hw_2_decoder_1_bit_comparator_2_c_i_plus_1_0), .ci1(hw_2_decoder_1_bit_comparator_2_c_i_plus_1_1),
    .xi(x3), .yi(y3), .c_i_plus_1_0(c40), .c_i_plus_1_1(c41));
  hw_2_decoder_1_bit_comparator hw_2_decoder_1_bit_comparator_2 (
    .ci0(hw_2_decoder_1_bit_comparator_3_c_i_plus_1_0), .ci1(hw_2_decoder_1_bit_comparator_3_c_i_plus_1_1),
    .xi(x2), .yi(y2), .c_i_plus_1_0(hw_2_decoder_1_bit_comparator_2_c_i_plus_1_0),
    .c_i_plus_1_1(hw_2_decoder_1_bit_comparator_2_c_i_plus_1_1));
  hw_2_decoder_1_bit_comparator hw_2_decoder_1_bit_comparator_3 (
    .ci0(hw_2_decoder_1_bit_comparator_4_c_i_plus_1_0), .ci1(hw_2_decoder_1_bit_comparator_4_c_i_plus_1_1),
    .xi(x1), .yi(y1), .c_i_plus_1_0(hw_2_decoder_1_bit_comparator_3_c_i_plus_1_0),
    .c_i_plus_1_1(hw_2_decoder_1_bit_comparator_3_c_i_plus_1_1));
  hw_2_decoder_1_bit_comparator hw_2_decoder_1_bit_comparator_4 (
    .ci0(c00), .ci1(c01), .xi(x0), .yi(y0), .c_i_plus_1_0(hw_2_decoder_1_bit_comparator_4_c_i_plus_1_0),
    .c_i_plus_1_1(hw_2_decoder_1_bit_comparator_4_c_i_plus_1_1));
endmodule
