// Digital circuit hw_2_decoder_1-bit_comparator.dig as structural Verilog
module hw_2_decoder_1_bit_comparator (
  input  [3:0] \input ,
  output c_i_plus_1_0,
  output c_i_plus_1_1
);

  wire decoder_1_out_0, decoder_1_out_1, decoder_1_out_2, decoder_1_out_3, decoder_1_out_4, decoder_1_out_5,
       decoder_1_out_6, decoder_1_out_7, decoder_1_out_8, decoder_1_out_9, decoder_1_out_10,
       decoder_1_out_11, decoder_1_out_12, decoder_1_out_13, decoder_1_out_14, decoder_1_out_15, or_1_out,
       or_3_out, or_4_out, or_6_out;

  Decoder #(.Selector_Bits(4)) decoder_1 (
    .sel(\input ), .out_0(decoder_1_out_0), .out_1(decoder_1_out_1), .out_2(decoder_1_out_2),
    .out_3(decoder_1_out_3), .out_4(decoder_1_out_4), .out_5(decoder_1_out_5), .out_6(decoder_1_out_6),
    .out_7(decoder_1_out_7), .out_8(decoder_1_out_8), .out_9(decoder_1_out_9), .out_10(decoder_1_out_10),
    .out_11(decoder_1_out_11), .out_12(decoder_1_out_12), .out_13(decoder_1_out_13),
    .out_14(decoder_1_out_14), .out_15(decoder_1_out_15));
  or or_1 (or_1_out, decoder_1_out_10, decoder_1_out_8, decoder_1_out_6, decoder_1_out_2);
  or or_2 (c_i_plus_1_0, or_3_out, or_1_out);
  or or_3 (or_3_out, decoder_1_out_15, decoder_1_out_14, decoder_1_out_12, decoder_1_out_11);
  or or_4 (or_4_out, decoder_1_out_7, decoder_1_out_5, decoder_1_out_4, decoder_1_out_1);
  or or_5 (c_i_plus_1_1, or_6_out, or_4_out);
  or or_6 (or_6_out, decoder_1_out_15, decoder_1_out_13, decoder_1_out_12, decoder_1_out_9);
endmodule
