// Digital circuit hw_2_nand_1-bit_comparator.dig as structural Verilog
module hw_2_nand_1_bit_comparator (
  input  ci0,
  input  ci1,
  input  xi,
  input  yi,
  output c_i_plus_1_0,
  output c_i_plus_1_1
);

  wire nand_1_out, nand_2_out, nand_3_out, nand_4_out, nand_5_out, nand_6_out, not_1_out, not_2_out;

  not not_1 (not_1_out, xi);
  not not_2 (not_2_out, yi);
  nand nand_1 (nand_1_out, ci0, not_2_out);
  nand nand_2 (nand_2_out, ci0, xi);
  nand nand_3 (nand_3_out, xi, not_2_out);
  nand nand_4 (nand_4_out, ci1, not_1_out);
  nand nand_5 (nand_5_out, ci1, yi);
  nand nand_6 (nand_6_out, not_1_out, yi);
  nand nand_7 (c_i_plus_1_0, nand_1_out, nand_2_out, nand_3_out);
  nand nand_8 (c_i_plus_1_1, nand_4_out, nand_5_out, nand_6_out);
endmodule
