// Digital circuit Braille.dig as structural Verilog
module Braille (
  input  A0,
  input  A1,
  input  A2,
  input  A3
);

  wire u_Braille_t, u_Braille_u, u_Braille_v, u_Braille_w, u_Braille_x, u_Braille_y;

  Braille #(.applicationType("GHDL")) u_Braille (
    .A(A3), .B(A2), .C(A1), .D(A0), .T(u_Braille_t), .U(u_Braille_u), .V(u_Braille_v), .W(u_Braille_w),
    .X(u_Braille_x), .Y(u_Braille_y));
  LED led_1 (.in(u_Braille_t));
  LED led_2 (.in(u_Braille_u));
  LED led_3 (.in(u_Braille_v));
  LED led_4 (.in(u_Braille_w));
  LED led_5 (.in(u_Braille_x));
  LED led_6 (.in(u_Braille_y));
endmodule

/* Code of Braille:
LIBRARY ieee;
USE ieee.std_logic_1164.all;
USE ieee.numeric_std.all;

entity Braille is
    port  (
        A, B, C, D: in std_logic;
        T, U, V, W, X, Y: out std_logic
    );
end Braille;

architecture Equations of Braille is
    begin   
        -- concurrent assignment statements
        T <= not A or B or C;
        U <= (not A and B and C) or (A and not B and not C) or (not A and not C and D) or (A and C and D);
        V <= (A and C) or (A and B);
        W <= (not A and not B and C) or (not A and C and not D) or (A and not C) or (A and B and D) or (B and not C and D);
        X <= (not A and C and D) or (not A and B and not D) or (A and not C and D) or (B and C and not D);
        Y <= 'Z';
    end Equations;
*/
