// Digital circuit q22_abff.dig as structural Verilog
module q22_abff (
  input  clk,
  input  A,
  input  B,
  output Q_plus
);

  wire and_1_out, and_2_out, not_1_out, rs_ff_1_nq;

  not not_1 (not_1_out, B);
  and and_1 (and_1_out, rs_ff_1_nq, A);
  and and_2 (and_2_out, not_1_out, Q_plus);
  RS_FF rs_ff_1 (.S(and_1_out), .C(clk), .R(and_2_out), .Q(Q_plus), .nQ(rs_ff_1_nq));

  // Notes on the sheet:
  //   SR -> JK -> AB
endmodule
